// Logisim project projeto-gtn-xtreme.circ as structural Verilog: 14 circuits, main circuit main
module main (
  output [7:0] Resposta_teste
);

  wire A, A_jogando, A_venceu, Av_A, Av_B, B, B_jogando, B_venceu, C_A, C_B, cfg, clk, Empate, FIM_DE_JOGO,
       Iniciar, jogando_X, jogando_Y, m0a_t, m0b_t, m1a_t, m1b_t, Reset, rgbled_1_p3, s0a_t, s0b_t, s1a_t,
       s1b_t, Soma_certa, X_certo, Y_certo;
  wire [3:0] M0a, M0b, M1a, M1b, Placar_A, Placar_B, S0a, S0b, S1a, S1b, V_A, V_B, X_atual, Y_atual;
  wire [7:0] b_t, r;

  Hex_Digit_Display hex_digit_display_1 (.value(M1a));  // open: dp
  Button button (.out(m1a_t));
  LED led_1 (.in(A_jogando));
  Hex_Digit_Display hex_digit_display_2 (.value(Placar_A));  // open: dp
  Hex_Digit_Display hex_digit_display_3 (.value(M0a));  // open: dp
  Button button_2 (.out(m0a_t));
  Hex_Digit_Display hex_digit_display_4 (.value(V_A));  // open: dp
  Button button_3 (.out(A));
  Button button_4 (.out(C_A));
  LED led_2 (.in(A_jogando));
  Hex_Digit_Display hex_digit_display_5 (.value(S1a));  // open: dp
  Hex_Digit_Display hex_digit_display_6 (.value(S0a));  // open: dp
  Button button_5 (.out(s1a_t));
  Button button_6 (.out(s0a_t));
  Button button_7 (.out(Av_A));
  Clock clock_1 (.out(clk));
  LED led_3 (.in(X_certo));
  LED led_4 (.in(A_venceu));
  LED led_5 (.in(Soma_certa));
  Hex_Digit_Display hex_digit_display_7 (.value(X_atual));  // open: dp
  LED led_6 (.in(jogando_X));
  Hex_Digit_Display hex_digit_display_8 (.value(Resposta_teste[3:0]));  // open: dp
  Hex_Digit_Display hex_digit_display_9 (.value(Resposta_teste[7:4]));  // open: dp
  LED led_7 (.in(FIM_DE_JOGO));
  LED led_8 (.in(Empate));
  LED led_9 (.in(cfg));
  Button button_8 (.out(Iniciar));
  // RGBLed #(.multibit("true")) rgbled_1: pin names not known; wires that end beside it: r, b_t, rgbled_1_p3
  Hex_Digit_Display hex_digit_display_10 (.value(Y_atual));  // open: dp
  LED led_10 (.in(jogando_Y));
  Button button_9 (.out(Reset));
  circuito_final circuito_final_1 (
    .clk(clk), .Reset(Reset), .Iniciar(Iniciar), .A(A), .B(B), .C_A(C_A), .C_B(C_B), .Av_A(Av_A),
    .Av_B(Av_B), .s0b(s0b_t), .s1a(s1a_t), .s1b(s1b_t), .m0a(m0a_t), .m0b(m0b_t), .m1a(m1a_t), .m1b(m1b_t),
    .cfg(cfg), .A_jogando(A_jogando), .B_jogando(B_jogando), .jogando_X(jogando_X), .jogando_Y(jogando_Y),
    .X_certo(X_certo), .Y_certo(Y_certo), .Soma_certa(Soma_certa), .r(r), .b_2(b_t), .X_atual(X_atual),
    .Y_atual(Y_atual), .V_A(V_A), .V_B(V_B), .M0a_2(M0a), .M1a_2(M1a), .S0b_2(S0b), .S1b_2(S1b), .M0b_2(M0b),
    .M1b_2(M1b), .Placar_A(Placar_A), .Placar_B(Placar_B), .FIM_DE_JOGO(FIM_DE_JOGO), .A_venceu(A_venceu),
    .Empate(Empate), .B_venceu(B_venceu), .s0a(s0a_t), .S1a_2(S1a), .S0a_2(S0a),
    .Resultado_8bit(Resposta_teste));
  LED led_11 (.in(B_venceu));
  LED led_12 (.in(Y_certo));
  Hex_Digit_Display hex_digit_display_11 (.value(M0b));  // open: dp
  Hex_Digit_Display hex_digit_display_12 (.value(M1b));  // open: dp
  Button button_10 (.out(m0b_t));
  Button button_11 (.out(m1b_t));
  Button button_12 (.out(B));
  Hex_Digit_Display hex_digit_display_13 (.value(Placar_B));  // open: dp
  Hex_Digit_Display hex_digit_display_14 (.value(S1b));  // open: dp
  Button button_13 (.out(s1b_t));
  Hex_Digit_Display hex_digit_display_15 (.value(V_B));  // open: dp
  Button button_14 (.out(Av_B));
  Button button_15 (.out(C_B));
  LED led_13 (.in(B_jogando));
  LED led_14 (.in(B_jogando));
  Hex_Digit_Display hex_digit_display_16 (.value(S0b));  // open: dp
  Button button_16 (.out(s0b_t));

  // Notes on the sheet:
  //   Jogador A
  //   CRONÔMETRO
  //   :
  //   Palpite A
  //   Guess The Number XTREME
  //   Vermelho: Perto
  //   Azul: Longe
  //   Jogador B
  //   CRONÔMETRO
  //   :
  //   Palpite B
endmodule

module circuito_final (
  input  clk,
  input  Reset,
  input  Iniciar,
  input  A,
  input  B,
  input  C_A,
  input  C_B,
  input  Av_A,
  input  Av_B,
  input  s0a,
  input  s0b,
  input  s1a,
  input  s1b,
  input  m0a,
  input  m0b,
  input  m1a,
  input  m1b,
  output cfg,
  output A_jogando,
  output B_jogando,
  output jogando_X,
  output jogando_Y,
  output X_certo,
  output Y_certo,
  output [7:0] Resultado_8bit,
  output Soma_certa,
  output [7:0] r,
  output [7:0] b_2,
  output [3:0] X_atual,
  output FIM_DE_JOGO,
  output [3:0] Y_atual,
  output [3:0] V_A,
  output A_venceu,
  output [3:0] V_B,
  output [3:0] S0a_2,
  output Empate,
  output [3:0] S1a_2,
  output B_venceu,
  output [3:0] M0a_2,
  output [3:0] M1a_2,
  output [3:0] S0b_2,
  output [3:0] S1b_2,
  output [3:0] M0b_2,
  output [3:0] M1b_2,
  output [3:0] Placar_A,
  output [3:0] Placar_B
);

  wire A15, Acerto, acertoOK, alguem15, autoAv, avA, Avancar, avB, avManual, B15, C_A_ok, C_B_ok, Fim_A,
       Fim_B, fimCond, iguais, IniciarOK, Jogando, Ligado, m0, m1, maiorA, maiorB, nFimA, nFimB, nFimJogo,
       nTempoAcabou, pontoA, pontoB, quemA, quemB, s0, s1, semTempo, semTempoA, semTempoB, tempoAcabou;

  Register #(.width(1), .Select("low")) register_1 (.D(1'b1), .en(1'b1), .Q(Ligado), .clk(IniciarOK), .clr(Reset));
  not not_1 (cfg, Ligado);
  not not_2 (nFimJogo, FIM_DE_JOGO);
  and and_1 (Jogando, Ligado, nFimJogo);
  and and_2 (Acerto, X_certo, Y_certo);
  and and_3 (avA, A_jogando, Av_A);
  and and_4 (avB, B_jogando, Av_B);
  or or_1 (avManual, avA, avB);
  or or_2 (s0, s0a, s0b);
  or or_3 (s1, s1a, s1b);
  or or_4 (m0, m0a, m0b);
  Register #(.width(1), .Select("low")) register_2 (.D(Acerto), .en(1'b1), .Q(acertoOK), .clk(Avancar), .clr(Reset));
  or or_5 (m1, m1a, m1b);
  not not_3 (quemB, quemA);
  and and_5 (pontoA, acertoOK, quemA);
  and and_6 (pontoB, acertoOK, quemB);
  or or_6 (alguem15, A15, B15);
  and and_7 (tempoAcabou, Fim_A, Fim_B);
  or or_7 (fimCond, alguem15, tempoAcabou);
  and and_8 (FIM_DE_JOGO, Ligado, fimCond);
  and and_9 (A_venceu, FIM_DE_JOGO, maiorA);
  and and_10 (Empate, FIM_DE_JOGO, iguais);
  and and_11 (B_venceu, FIM_DE_JOGO, maiorB);
  Register #(.width(1), .Select("low")) register_3 (.D(A_jogando), .en(1'b1), .Q(quemA), .clk(Avancar), .clr(Reset));
  CORE CORE (
    .C_A(C_A_ok), .C_B(C_B_ok), .V_A(V_A), .V_B(V_B), .Jogando(Jogando), .Fim_A(Fim_A), .Fim_B(Fim_B),
    .Avancar(Avancar), .Acerto(Acerto), .Reset(Reset), .A_jogando(A_jogando), .B_jogando(B_jogando),
    .jogando_X(jogando_X), .jogando_Y(jogando_Y), .X_atual(X_atual), .Y_atual(Y_atual), .X_certo(X_certo),
    .Y_certo(Y_certo), .Soma_certa(Soma_certa), .r(r), .b(b_2), .Resultado_8bit(Resultado_8bit));
  Cronometro Cronometro_A (
    .clk(clk), .jogando(A_jogando), .cfg(cfg), .reset(Reset), .s0(s0), .s1(s1), .m0(m0), .m1(m1),
    .FimC(Fim_A), .S0c(S0a_2), .S1c(S1a_2), .M0c(M0a_2), .M1c(M1a_2));
  Cronometro Cronometro_B (
    .clk(clk), .jogando(B_jogando), .cfg(cfg), .reset(Reset), .s0(s0), .s1(s1), .m0(m0), .m1(m1),
    .FimC(Fim_B), .S0c(S0b_2), .S1c(S1b_2), .M0c(M0b_2), .M1c(M1b_2));
  Contador cntVA (.Enable(1'b1), .Clock(A), .Reset(Reset), .out_4(V_A));
  Contador cntVB (.Enable(1'b1), .Clock(B), .Reset(Reset), .out_4(V_B));
  Contador placA (.Enable(1'b1), .Clock(pontoA), .Reset(Reset), .out_4(Placar_A));
  Contador placB (.Enable(1'b1), .Clock(pontoB), .Reset(Reset), .out_4(Placar_B));
  comparador_4b comparador_4b_1 (.A(4'b1111), .B(Placar_A), .Igual(A15));
  comparador_4b comparador_4b_2 (.A(4'b1111), .B(Placar_B), .Igual(B15));
  Comparator #(.width(4), .mode("unsigned")) comparator_1 (
    .a(Placar_A), .b(Placar_B), .gt(maiorA), .eq(iguais), .lt(maiorB));
  not not_4 (nTempoAcabou, tempoAcabou);
  not not_5 (nFimA, Fim_A);
  not not_6 (nFimB, Fim_B);
  and and_12 (IniciarOK, Iniciar, nTempoAcabou);
  and and_13 (C_A_ok, C_A, nFimA);
  and and_14 (C_B_ok, C_B, nFimB);
  and and_15 (semTempoA, A_jogando, Fim_A);
  and and_16 (semTempoB, B_jogando, Fim_B);
  or or_8 (semTempo, semTempoA, semTempoB);
  and and_17 (autoAv, clk, semTempo);
  or or_9 (Avancar, avManual, autoAv);

  // Other names for the same wires on the sheet: b_t[7:0] = b_2; FimJogo = FIM_DE_JOGO; M0a_t[3:0] = M0a_2;
  //   M0b_t[3:0] = M0b_2; M1a_t[3:0] = M1a_2; M1b_t[3:0] = M1b_2; S0a_t[3:0] = S0a_2; S0b_t[3:0] = S0b_2;
  //   S1a_t[3:0] = S1a_2; S1b_t[3:0] = S1b_2
endmodule

module Registrador4 (
  input  [3:0] D,
  input  Enable,
  input  Clock,
  input  Reset,
  output [3:0] Q
);

  Register #(.width(4), .Select("low")) register_1 (.D(D), .en(Enable), .Q(Q), .clk(Clock), .clr(Reset));
endmodule

module Contador (
  input  Enable,
  input  Clock,
  input  Reset,
  output [3:0] out_4
);

  Counter #(.width(4), .max('hf)) counter_1 (
    .count(Enable), .Q(out_4), .clk(Clock), .clr(Reset), .down(1'b0));  // open: load, D, carry, preset
endmodule

module Comparador_5b (
  input  [4:0] A,
  input  [4:0] B,
  output Igual
);

  Comparator #(.width(5)) comparator_1 (.a(A), .b(B), .eq(Igual));  // open: gt, lt
endmodule

module Somador4b5b (
  input  [3:0] A,
  input  [3:0] B,
  output [4:0] out_3
);

  Adder #(.width(4)) adder_1 (.a(A), .b(B), .out(out_3[3:0]), .cout(out_3[4]));  // open: cin
endmodule

module Diferenca_5b (
  input  [4:0] A,
  input  [4:0] B,
  output [4:0] DIFF
);

  wire SEL;
  wire [4:0] DAB, DBA;

  Multiplexer #(.width(5), .enable("false")) multiplexer_1 (.in0(DAB), .in1(DBA), .out(DIFF), .sel(SEL));
  Subtractor #(.width(5)) subtractor_1 (.a(A), .b(B), .out(DAB), .bin(1'b0), .bout(SEL));
  Subtractor #(.width(5)) subtractor_2 (.a(B), .b(A), .out(DBA), .bin(1'b0));  // open: bout
endmodule

module cores_5b (
  input  [4:0] a,
  output [7:0] out_2,
  output [7:0] out_3
);

  wire [7:0] bit_extender_1_out, shifter_1_out;

  assign bit_extender_1_out = {{3{1'b0}}, a};  // Bit_Extender bit_extender_1
  Shifter shifter_1 (.in(bit_extender_1_out), .\dist (3'b011), .out(shifter_1_out));
  assign out_2 = shifter_1_out | 8'h7;  // OR_Gate or_1, 8 bits wide
  assign out_3 = ~out_2;  // NOT_Gate not_1, 8 bits wide
endmodule

module GTN_X (
  input  Confirmar,
  input  Novo,
  input  [3:0] X,
  input  [3:0] Y,
  output [7:0] b,
  output [7:0] r,
  output X_2,
  output Y_2,
  output S,
  output [7:0] Resposta_8bit
);

  wire comparador_4b_1_igual, comparador_4b_2_igual, comparador_5b_1_igual;
  wire [4:0] diferenca_5b_1_diff, somador4b5b_1_out_3, somador4b5b_2_out_3;
  wire [7:0] bit_extender_1_out, cores_5b_1_out_2, cores_5b_1_out_3;

  Random random_1 (.clk(Novo), .out(Resposta_8bit));  // open: next, clr
  assign bit_extender_1_out = {{7{Confirmar}}, Confirmar};  // Bit_Extender bit_extender_1
  and and_1 (X_2, Confirmar, comparador_4b_1_igual);
  comparador_4b comparador_4b_1 (.A(Resposta_8bit[7:4]), .B(X), .Igual(comparador_4b_1_igual));
  Somador4b5b somador4b5b_1 (.A(Resposta_8bit[3:0]), .B(Resposta_8bit[7:4]), .out_3(somador4b5b_1_out_3));
  Somador4b5b somador4b5b_2 (.A(X), .B(Y), .out_3(somador4b5b_2_out_3));
  and and_2 (S, Confirmar, comparador_5b_1_igual);
  and and_3 (Y_2, Confirmar, comparador_4b_2_igual);
  comparador_4b comparador_4b_2 (.A(Resposta_8bit[3:0]), .B(Y), .Igual(comparador_4b_2_igual));
  Comparador_5b comparador_5b_1 (.A(somador4b5b_1_out_3), .B(somador4b5b_2_out_3), .Igual(comparador_5b_1_igual));
  assign b = bit_extender_1_out & cores_5b_1_out_2;  // AND_Gate and_4, 8 bits wide
  assign r = cores_5b_1_out_3 & bit_extender_1_out;  // AND_Gate and_5, 8 bits wide
  cores_5b cores_5b_1 (.a(diferenca_5b_1_diff), .out_2(cores_5b_1_out_2), .out_3(cores_5b_1_out_3));
  Diferenca_5b diferenca_5b_1 (.A(somador4b5b_1_out_3), .B(somador4b5b_2_out_3), .DIFF(diferenca_5b_1_diff));
endmodule

module comparador_4b (
  input  [3:0] A,
  input  [3:0] B,
  output Igual
);

  Comparator #(.width(4)) comparator_1 (.a(A), .b(B), .eq(Igual));  // open: gt, lt
endmodule

module Digito (
  input  clk,
  input  BTN,
  input  EN,
  input  cfg,
  input  RESET,
  input  [3:0] MAX,
  output [3:0] Q,
  output ZERO
);

  wire ATMAX, clkd, enr;
  wire [3:0] D, Dcfg, DEC, Drun, INC;

  Multiplexer #(.width(4)) multiplexer_1 (.in0(DEC), .in1(MAX), .out(Drun), .sel(ZERO));  // open: en
  Multiplexer #(.width(4)) multiplexer_2 (.in0(INC), .in1(4'b0000), .out(Dcfg), .sel(ATMAX));  // open: en
  Adder #(.width(4)) adder_1 (.a(Q), .b(4'b0001), .out(INC), .cin(1'b0));  // open: cout
  Subtractor #(.width(4)) subtractor_1 (.a(Q), .b(4'b0001), .out(DEC), .bin(1'b0));  // open: bout
  Comparator #(.width(4)) comparator_1 (.a(Q), .b(4'b0000), .eq(ZERO));  // open: gt, lt
  Comparator #(.width(4)) comparator_2 (.a(Q), .b(MAX), .eq(ATMAX));  // open: gt, lt
  Multiplexer #(.width(4)) multiplexer_3 (.in0(Drun), .in1(Dcfg), .out(D), .sel(cfg));  // open: en
  Multiplexer multiplexer_4 (.in0(clk), .in1(BTN), .out(clkd), .sel(cfg));  // open: en
  Multiplexer multiplexer_5 (.in0(EN), .in1(1'b1), .out(enr), .sel(cfg));  // open: en
  Register #(.width(4), .Select("low")) Qreg (.D(D), .en(enr), .Q(Q), .clk(clkd), .clr(RESET));
endmodule

module Cronometro (
  input  clk,
  input  jogando,
  input  cfg,
  input  reset,
  input  s0,
  input  s1,
  input  m0,
  input  m1,
  output FimC,
  output [3:0] S0c,
  output [3:0] S1c,
  output [3:0] M0c,
  output [3:0] M1c
);

  wire EN_M0, EN_M1, EN_S1, G, NCFG, NFIM, Z_M0, Z_M1, Z_S0, Z_S1;

  Digito Dig_S0 (.clk(clk), .BTN(s0), .EN(G), .cfg(cfg), .RESET(reset), .MAX(4'b1001), .Q(S0c), .ZERO(Z_S0));
  Digito Dig_S1 (.clk(clk), .BTN(s1), .EN(EN_S1), .cfg(cfg), .RESET(reset), .MAX(4'b0101), .Q(S1c), .ZERO(Z_S1));
  not not_1 (NCFG, cfg);
  not not_2 (NFIM, FimC);
  Digito Dig_M0 (.clk(clk), .BTN(m0), .EN(EN_M0), .cfg(cfg), .RESET(reset), .MAX(4'b1001), .Q(M0c), .ZERO(Z_M0));
  Digito Dig_M1 (.clk(clk), .BTN(m1), .EN(EN_M1), .cfg(cfg), .RESET(reset), .MAX(4'b0101), .Q(M1c), .ZERO(Z_M1));
  and and_1 (G, jogando, NCFG, NFIM);
  and and_2 (EN_S1, G, Z_S0);
  and and_3 (EN_M0, G, Z_S0, Z_S1);
  and and_4 (EN_M1, G, Z_S0, Z_S1, Z_M0);
  and and_5 (FimC, Z_S0, Z_S1, Z_M0, Z_M1);

  // Other names for the same wires on the sheet: FIM = FimC; JOG = jogando; Q_M0[3:0] = M0c; Q_M1[3:0] = M1c;
  //   Q_S0[3:0] = S0c; Q_S1[3:0] = S1c
endmodule

module CORE (
  input  C_A,
  input  C_B,
  input  [3:0] V_A,
  input  [3:0] V_B,
  input  Jogando,
  input  Fim_A,
  input  Fim_B,
  input  Avancar,
  input  Acerto,
  input  Reset,
  output [7:0] Resultado_8bit,
  output X_certo,
  output Y_certo,
  output Soma_certa,
  output [7:0] r,
  output [7:0] b,
  output [3:0] X_atual,
  output [3:0] Y_atual,
  output A_jogando,
  output B_jogando,
  output jogando_X,
  output jogando_Y
);

  wire cA_t, cB_t, CONF, NOVO, RESU;
  wire [3:0] VSEL;

  and and_1 (cA_t, A_jogando, C_A);
  and and_2 (cB_t, B_jogando, C_B);
  or or_1 (CONF, cA_t, cB_t);
  Register #(.width(1), .Select("low")) register_1 (.D(Acerto), .en(1'b1), .Q(NOVO), .clk(Avancar), .clr(Reset));
  ESTADO_CORE estado_core_1 (
    .Avancar(Avancar), .Reset(Reset), .Jogando(Jogando), .fim_A(Fim_A), .fim_B(Fim_B), .A_jogando(A_jogando),
    .B_jogando(B_jogando), .jogando_X(jogando_X), .jogando_Y(jogando_Y), .Resultado(RESU));  // open: Estado_atual
  Multiplexer #(.width(4), .enable("false")) multiplexer_1 (.in0(V_A), .in1(V_B), .out(VSEL), .sel(B_jogando));
  Registrador4 RegX (.D(VSEL), .Enable(jogando_X), .Clock(CONF), .Reset(Reset), .Q(X_atual));
  Registrador4 RegY (.D(VSEL), .Enable(jogando_Y), .Clock(CONF), .Reset(Reset), .Q(Y_atual));
  GTN_X GTN_X (
    .Confirmar(RESU), .Novo(NOVO), .X(X_atual), .Y(Y_atual), .X_2(X_certo), .Y_2(Y_certo), .S(Soma_certa),
    .r(r), .b(b), .Resposta_8bit(Resultado_8bit));

  // Other names for the same wires on the sheet: Ajog = A_jogando; AV = Avancar; Bjog = B_jogando; CA = C_A; CB = C_B;
  //   FA = Fim_A; FB = Fim_B; JOG = Jogando; jX = jogando_X; jY = jogando_Y; RST = Reset; VA[3:0] = V_A;
  //   VB[3:0] = V_B; Xq[3:0] = X_atual; Yq[3:0] = Y_atual
endmodule

module ESTADO_CORE (
  input  Avancar,
  input  Reset,
  input  fim_A,
  input  fim_B,
  input  Jogando,
  output [2:0] Estado_atual,
  output Resultado,
  output A_jogando,
  output B_jogando,
  output jogando_X,
  output jogando_Y
);

  wire AJOG, BJOG, D0, D1, D2, E0, E01, E1, E2, E3, E4, E5, E6, E7, E23, E45, JX, JY, nFA, nFB;
  wire [3:0] bit_extender_1_out;

  Register #(.width(3), .Select("low")) Estado (
    .D({D2, D1, D0}), .en(Jogando), .Q(Estado_atual), .clk(Avancar), .clr(Reset));
  Multiplexer #(.select(3), .enable("false")) multiplexer_1 (
    .in0(1'b0), .in1(1'b0), .in2(1'b1), .in3(fim_B), .in4(1'b1), .in5(1'b0), .in6(nFA), .in7(1'b1), .out(D0),
    .sel(Estado_atual));
  Multiplexer #(.select(3), .enable("false")) multiplexer_2 (
    .in0(1'b1), .in1(1'b1), .in2(1'b1), .in3(1'b0), .in4(1'b0), .in5(1'b1), .in6(1'b0), .in7(1'b0), .out(D1),
    .sel(Estado_atual));
  Hex_Digit_Display hex_digit_display_1 (.value(bit_extender_1_out));  // open: dp
  assign bit_extender_1_out = {{1{1'b0}}, Estado_atual};  // Bit_Extender bit_extender_1
  Multiplexer #(.select(3), .enable("false")) multiplexer_3 (
    .in0(1'b0), .in1(1'b0), .in2(1'b0), .in3(nFB), .in4(1'b1), .in5(1'b1), .in6(fim_A), .in7(1'b0), .out(D2),
    .sel(Estado_atual));
  Decoder #(.select(3), .enable("false")) decoder_1 (
    .out0(E0), .out1(E1), .out2(E2), .out3(E3), .out4(E4), .out5(E5), .out6(E6), .out7(E7), .sel(Estado_atual));
  or or_1 (E01, E0, E1);
  or or_2 (E23, E2, E3);
  or or_3 (AJOG, E01, E23);
  or or_4 (E45, E4, E5);
  or or_5 (BJOG, E45, E6);
  or or_6 (JX, E01, E4);
  not not_1 (nFA, fim_A);
  not not_2 (nFB, fim_B);
  or or_7 (JY, E2, E5);
  or or_8 (Resultado, E3, E6);
  and and_1 (A_jogando, AJOG, Jogando);
  and and_2 (B_jogando, BJOG, Jogando);
  and and_3 (jogando_X, JX, Jogando);
  and and_4 (jogando_Y, JY, Jogando);

  // Other names for the same wires on the sheet: FA = fim_A; FB = fim_B; JOG = Jogando; Q[2:0] = Estado_atual
endmodule
